# Fritzing sketch SediNetCamv2 (saved by Fritzing 0.9.6b)
breadboards: 1

parts:
  Mod1 = Raspberry Pi 4B
  S2 = Round Pushbutton
  Part1 = Adafruit PCF8523 RTC [part_number="Adafruit #3295"]
  Part2 = Adafruit Ultimate GPS v3 [part_number="Adafruit #746"]
  U1 = WS2812 RGB LED strip

nets:
  VCC: Mod1.3V3, Part1.VCC, Part2.3.3V, U1.VCC
  N1: Mod1.GPIO2, Part1.SDA
  N2: Mod1.GPIO3, Part1.SCL
  GND: Mod1.GND, S2.leg1, Part1.GND, Part2.GND, U1.GND
  N3: Mod1.GPIO14, Part2.TX
  N4: Mod1.GPIO15, Part2.RX
  N5: Mod1.GPIO18, U1.DIN
  N6: Mod1.GPIO26, Mod1.GPIO20, S2.leg0

notes:
  RTC and GPS may be different from BOM, just make sure RTC is I2C and GPS is UART. LED strip will be same connections

custom parts:
  Adafruit PCF8523 RTC: This is a great battery-backed real time clock (RTC) that allows your microcontroller project to keep track of time even if it is reprogrammed, or if the power is lost. Perfect for datalogging, clock-building, time stamping, timers and alarms, etc. Equipped with PCF8523 RTC - it can run from 3.3V or 5V power & logic! Works great with an Arduino using our RTC library, with CircuitPython or with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
  Adafruit Ultimate GPS v3: We carry a few different GPS modules here in the Adafruit shop, but none that satisfied our every desire - that's why we designed this little GPS breakout board. We believe this is the Ultimate GPS module, so we named it that. It's got everything you want and more: -165 dBm sensitivity, 10 Hz updates, 66 channels 5V friendly design and only 20mA current draw Breadboard friendly + two mounting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
  WS2812 RGB LED strip: WS2812 strip
