# Fritzing sketch sandcamv2 (saved by Fritzing 0.9.6b)

parts:
  Mod1 = Raspberry Pi 4B
  Part1 = Adafruit Ultimate GPS HAT [part_number="Adafruit #2324"]
  U1 = WS2812 RGB LED strip

nets:
  3V3: Mod1.3V3, Part1.3.3V
  5V: Mod1.5V, Part1.5.0V, U1.VCC
  N1: Mod1.GPIO2, Part1.SDA
  N2: Mod1.GPIO3, Part1.SCL
  GND: Mod1.GND, Part1.GND, U1.GND
  N3: Mod1.GPIO4, Part1.GPIO4
  N4: Mod1.GPIO14, Part1.TXD
  N5: Mod1.GPIO15, Part1.RXD
  N6: Mod1.GPIO17, Part1.GPIO17
  N7: Mod1.GPIO18, Part1.GPIO18, U1.DIN
  N8: Mod1.GPIO27, Part1.GPIO27
  N9: Mod1.GPIO22, Part1.GPIO22
  N10: Mod1.GPIO23, Part1.GPIO23
  N11: Mod1.GPIO24, Part1.GPIO24
  N12: Mod1.GPIO10, Part1.SPI_MOSI
  N13: Mod1.GPIO9, Part1.SPI_MISO
  N14: Mod1.GPIO25, Part1.GPIO25
  N15: Mod1.GPIO11, Part1.SPI_SCLK
  N16: Mod1.GPIO8, Part1.SPI_CE0
  N17: Mod1.GPIO7, Part1.SPI_CE1
  N18: Mod1.ID_SD, Part1.EEDATA
  N19: Mod1.ID_SC, Part1.EECLK
  N20: Mod1.GPIO5, Part1.GPIO5
  N21: Mod1.GPIO6, Part1.GPIO6
  N22: Mod1.GPIO12, Part1.GPIO12
  N23: Mod1.GPIO13, Part1.GPIO13
  N24: Mod1.GPIO19, Part1.GPIO19
  N25: Mod1.GPIO16, Part1.GPIO16
  N26: Mod1.GPIO26, Part1.GPIO26
  N27: Mod1.GPIO20, Mod1.TR02_TAP, Part1.GPIO20
  N28: Mod1.GPIO21, Mod1.TR03_TAP, Part1.GPIO21

notes:
  Raspberry Pi 7-in LCD
  TouchScreen
  5v to 5v
  GND to GND

custom parts:
  Adafruit Ultimate GPS HAT: It's 10PM, do you know where your Raspberry Pi is? If you had this GPS HAT, you would! This new HAT from Adafruit adds our celebrated Ultimate GPS on it, so you can add precision time and location to your Raspberry Pi Model A+, B+, or Pi 2. Does not work with the Pi 3 at this time Here's the low-down on the GPS module: -165 dBm sensitivity, 10 Hz updates, 66 channels Only 20mA current draw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
  WS2812 RGB LED strip: WS2812 strip
